# Fritzing sketch sketch (saved by Fritzing 0.9.3b)
breadboards: 2

parts:
  J1 = STM32 Nucleo boards
  Nokia_5110_LCD_Module1 = Nokia 5110 LCD  # not connected
  J2 = Piezo Speaker  # not connected
  J3 = Basic Force Sensing Resistor (FSR) [package=THT]  # not connected
  R1 = Photocell (LDR) [package=THT]
  T1 = LM35 Temperature Sensor [package="TO92 [THT]"]
  Part1 = Black Joystick KY-023
  R4 = Resistor [tolerance=±5% resistance=10k package="0603 [SMD]"]  # not connected
  R5 = Resistor [tolerance=±5% resistance=10k package="0603 [SMD]"]  # not connected
  R6 = TRIMPOT [package=3386u]
  ON_OFF = Pushbutton [package="[THT]"]  # not connected
  RIGHT = Pushbutton [package="[THT]"]  # not connected
  LEFT = Pushbutton [package="[THT]"]  # not connected
  R11 = Resistor [tolerance=±5% resistance=10k package="0603 [SMD]"]  # not connected
  R12 = Resistor [tolerance=±5% resistance=10k package="0603 [SMD]"]  # not connected
  R13 = Resistor [tolerance=±5% resistance=10k package="0603 [SMD]"]
  R14 = Resistor [tolerance=±5% resistance=220 package="0603 [SMD]"]
  LED9 = LED - 3mm [color="Blue (430nm)" current=0.030 package="3 mm [THT]"]
  LED16 = LED - 3mm [color="Blue (430nm)" current=0.030 package="3 mm [THT]"]
  LED17 = LED - 3mm [color="Blue (430nm)" current=0.030 package="3 mm [THT]"]
  LED18 = LED - 3mm [color="Yellow (595nm)" current=0.030 package="3 mm [THT]"]
  LED19 = LED - 3mm [color="Yellow (595nm)" current=0.030 package="3 mm [THT]"]
  LED20 = LED - 3mm [color="Green (555nm)" current=0.030 package="3 mm [THT]"]
  LED21 = LED - 3mm [color="Green (555nm)" current=0.030 package="3 mm [THT]"]
  LED22 = LED - 3mm [color="Green (555nm)" current=0.030 package="3 mm [THT]"]
  LED23 = LED - 3mm [color="Red (633nm)" current=0.030 package="3 mm [THT]"]
  R20 = Resistor [tolerance=±5% resistance=220 package="0603 [SMD]"]
  R21 = Resistor [tolerance=±5% resistance=220 package="0603 [SMD]"]
  R22 = Resistor [tolerance=±5% resistance=220 package="0603 [SMD]"]
  R23 = Resistor [tolerance=±5% resistance=220 package="0603 [SMD]"]
  R24 = Resistor [tolerance=±5% resistance=220 package="0603 [SMD]"]
  R25 = Resistor [tolerance=±5% resistance=220 package="0603 [SMD]"]
  R26 = Resistor [tolerance=±5% resistance=220 package="0603 [SMD]"]
  R27 = Resistor [tolerance=±5% resistance=220 package="0603 [SMD]"]

nets:
  N1: J1.PC8, LED22.anode
  N2: J1.PC6, LED21.anode
  N3: J1.PA12, LED18.anode
  N4: J1.PA11, LED19.anode
  N5: J1.PB15, LED9.anode
  N6: J1.PB14, LED16.anode
  N7: J1.PB13, LED17.anode
  N8: J1.PC9, LED23.anode
  N9: J1.PB8, LED20.anode
  N10: J1.PA0, T1.Vout
  N11: J1.PA1, R1.pin_1, R13.Pin_0
  N12: J1.PC0, R6.WIPER
  N13: J1.PC2, Part1.VRx
  N14: J1.PC3, Part1.VRy
  N15: R1.pin_0, T1.+Vs
  GND: T1.GND, Part1.GND, R13.Pin_1, R14.Pin_1, R20.Pin_1, R21.Pin_1, R22.Pin_1, R23.Pin_1, R24.Pin_1, R25.Pin_1, R26.Pin_1, R27.Pin_1
  N16: R14.Pin_0, LED9.cathode
  N17: LED16.cathode, R20.Pin_0
  N18: LED17.cathode, R21.Pin_0
  N19: LED18.cathode, R22.Pin_0
  N20: LED19.cathode, R23.Pin_0
  N21: LED20.cathode, R24.Pin_0
  N22: LED21.cathode, R25.Pin_0
  N23: LED22.cathode, R26.Pin_0
  N24: LED23.cathode, R27.Pin_0

custom parts:
  Nokia 5110 LCD: Nokia 5110 Graphic 84*48 LCD module such as the Sparkfun LCD-10168 or the clones from Ebay. There is example code for the Arduino available from the Sparkfun site in https://learn.sparkfun.com/tutorials/graphic-lcd-hookup-guide This is a 3.3V device, if you are running it from a 5V micro you need a 5V tolorant level translator such as the 74ahc367 to protect the signal imputs. Rafa G. did a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
  Black Joystick KY-023: Description: The joystick is a combination of 2 analoog potentiometer and a digital switch. Arduino GND --> Module pin - Arduino +5V --> Module pin +5V Arduino Analoog 0 --> Module VRx Arduino Analoog 1 --> Module VRy Arduino Digital --> Module SW Dimensions: 1" x 1.25"
